# Fritzing sketch placa-conexoes-externas-bitdoglab (saved by Fritzing 0.9.3b)
circuit board: 5cm x 9cm

parts:
  SERVO1 = Tower Pro SG90 servo [part_number=101246]
  LED1 = RGB LED (com. cathode, rgb) [package="5 mm [THT]"]
  LDR = Photocell (LDR) [package=THT]
  R_10K = Resistor [tolerance=±10% resistance=10k package=THT]
  R_220 = Resistor [tolerance=±5% resistance=220 package=THT]
  R_220_2 = Resistor [tolerance=±5% resistance=220 package=THT]
  GY1 = MPU-6050 Board GY-521 [form="♀ (female)" package=THT]
  R_220_3 = Resistor [tolerance=±5% resistance=220 package=THT]
  PAD2 = Pad Oval 5x3 mm - Anel 1 mm
  PAD3 = Pad Oval 5x3 mm - Anel 1 mm
  PAD5 = Pad Oval 5x3 mm - Anel 1 mm
  PAD6 = Pad Oval 5x3 mm - Anel 1 mm
  PAD7 = Pad Oval 5x3 mm - Anel 1 mm
  PAD8 = Pad Oval 5x3 mm - Anel 1 mm
  PAD9 = Pad Oval 5x3 mm - Anel 1 mm
  PAD10 = Pad Oval 5x3 mm - Anel 1 mm
  PAD11 = Pad Oval 5x3 mm - Anel 1 mm
  PAD12 = Pad Oval 5x3 mm - Anel 1 mm
  PAD13 = Pad Oval 5x3 mm - Anel 1 mm
  PAD14 = Pad Oval 5x3 mm - Anel 1 mm
  HC-SR04_Sensor_1 = HC-SR04 Ultrasonic Distance Sensor
  PAD15 = Pad Oval 5x3 mm - Anel 1 mm
  PAD16 = Pad Oval 5x3 mm - Anel 1 mm
  PAD17 = Pad Oval 5x3 mm - Anel 1 mm
  PAD18 = Pad Oval 5x3 mm - Anel 1 mm
  PAD19 = Pad Oval 5x3 mm - Anel 1 mm
  PAD20 = Pad Oval 5x3 mm - Anel 1 mm
  PAD21 = Pad Oval 5x3 mm - Anel 1 mm
  PAD22 = Pad Oval 5x3 mm - Anel 1 mm
  PAD23 = Pad Oval 5x3 mm - Anel 1 mm
  PAD24 = Pad Oval 5x3 mm - Anel 1 mm
  PAD25 = Pad Oval 5x3 mm - Anel 1 mm
  PAD26 = Pad Oval 5x3 mm - Anel 1 mm
  DHT1 = Humidity and Temperature Sensor DHT11
  R_10K1 = Resistor [tolerance=±10% resistance=10k package=THT]

nets:
  N1: SERVO1.Signal, PAD15.Pad, PAD24.Pad
  N2: SERVO1.+5V, PAD19.Pad, PAD21.Pad
  GND: SERVO1.GND, LED1.common_cathode, LDR.pin_0, GY1.pin2, PAD8.Pad, PAD14.Pad, HC-SR04_Sensor_1.GND, PAD17.Pad, PAD23.Pad, DHT1.GND_2
  N3: LED1.red_anode, R_220.Pin_1
  N4: LED1.green_anode, R_220_3.Pin_1
  N5: LED1.blue_anode, R_220_2.Pin_1
  N6: LDR.pin_1, R_10K.Pin_1, PAD6.Pad, PAD12.Pad
  VCC: R_10K.Pin_0, GY1.pin1, PAD2.Pad, PAD9.Pad, HC-SR04_Sensor_1.VCC, DHT1.Vcc, R_10K1.Pin_0
  N7: R_220.Pin_0, PAD18.Pad, PAD26.Pad
  N8: R_220_2.Pin_0, PAD16.Pad, PAD25.Pad
  N9: GY1.pin3, PAD5.Pad, PAD11.Pad, HC-SR04_Sensor_1.TRIG_/_SCL
  N10: GY1.pin4, PAD3.Pad, PAD10.Pad, HC-SR04_Sensor_1.ECHO_/_SDA
  N11: R_220_3.Pin_0, PAD20.Pad, PAD22.Pad
  N12: PAD7.Pad, PAD13.Pad, DHT1.Data-signal, R_10K1.Pin_1

notes:
  Vermelho
  Verde
  Azul
  3.3V
  GND
  Servo
  Distancia
  -
  +
  HC-SR04 I2C
  Luz
  LED RGB
  R
  B
  G
  Acelerometro
  MPU6050
  VCC
  SDA
  SCL
  5V
  T°/UR
  (+)
  (-)
  Motor
  S
  Dados
  R 10K
  DHT11

custom parts:
  Tower Pro SG90 servo: Original file by John De Cristofaro http://www.adafruit.com/products/1449 Adafruit Feedback Servo (Small) Edited by: e-radionica.com 28/9/2015
  MPU-6050 Board GY-521: Acelerometro y Giroscopio MPU-6050 Board GY-521
  Pad Oval 5x3 mm - Anel 1 mm: Pad THT oval de tamanho fixo para uso no Fritzing. Abertura visual interna de 5 x 3 mm, anel de cobre de 1 mm, dimensão externa de 7 x 5 mm.
  HC-SR04 Ultrasonic Distance Sensor: The HC-SR04 is an ultrasonic distance sensor. It is capable of providing measurement for ranges of 2cm to 400cm. The module operates at 5V.
  Humidity and Temperature Sensor DHT11: Digital relative humidity & temperature sensor DHT11

// code stored in the sketch: Untitled2.ino

